# Fritzing sketch de-elec-simple1 (saved by Fritzing 0.9.3b)
circuit board: 8.46667cm x 5.64444cm
breadboards: 1

parts:
  7_Segment1 = 7 Segment Display
  Composant1 = Arduino Uno (Rev3)
  R1 = Resistor [tolerance=±5% resistance=10k package=THT]
  R2 = Resistor [tolerance=±5% resistance=1k package=THT]
  R3 = Resistor [tolerance=±5% resistance=1k package=THT]
  R4 = Resistor [tolerance=±5% resistance=1k package=THT]
  R5 = Resistor [tolerance=±5% resistance=1k package=THT]
  R6 = Resistor [tolerance=±5% resistance=1k package=THT]
  R7 = Resistor [tolerance=±5% resistance=1k package=THT]
  R8 = Resistor [tolerance=±5% resistance=1k package=THT]
  R9 = Resistor [tolerance=±5% resistance=1k package=THT]
  R10 = Resistor [tolerance=±5% resistance=1k package=THT]
  LED1 = smd LED [color="Green (565nm)" package="0805 [SMD]"]
  S1 = Pushbutton [package="[SMD]"]

nets:
  N1: 7_Segment1.Segment_E, R7.Pin_1
  N2: 7_Segment1.Segment_D, R6.Pin_1
  N3: 7_Segment1.common_cathode, Composant1.GND, R1.Pin_0, R10.Pin_0
  N4: 7_Segment1.Segment_C, R9.Pin_0
  N5: 7_Segment1.Segment_DP, R8.Pin_0
  N6: 7_Segment1.Segment_B, R5.Pin_0
  N7: 7_Segment1.Segment_A, R4.Pin_0
  N8: 7_Segment1.Segment_F, R2.Pin_1
  N9: 7_Segment1.Segment_G, R3.Pin_1
  N10: Composant1.D8, R5.Pin_1
  N11: Composant1.D9_PWM, R8.Pin_1
  N12: Composant1.D10_PWM/SS, LED1.anode
  N13: Composant1.D11_PWM/MOSI, R1.Pin_1, S1.Pin_3, S1.Pin_4
  N14: Composant1.D2, R7.Pin_0
  N15: Composant1.D3_PWM, R3.Pin_0
  N16: Composant1.D4, R6.Pin_0
  N17: Composant1.D5_PWM, R2.Pin_0
  N18: Composant1.D6_PWM, R9.Pin_1
  N19: Composant1.D7, R4.Pin_1
  N20: Composant1.5V, S1.Pin_1, S1.Pin_2
  N21: R10.Pin_1, LED1.cathode

// code stored in the sketch: de-elec-simple1.ino
/**
 * Un dé hexadécimal électronique 
 * tirant des nombres de 0 à F,
 * avec un afficheur 7 segments.
 */
#include "SevenSegmentDisplay.hpp"

using D7 = SevenSegmentDisplay;			// alias
using time_t = decltype(millis());

// Brochage
const int ledPin = 10;    // Broche permettant la fonction lancé de dé
const int swPin = 11;     // Broche lisant l'appui sur le bouton

// Afficheur 7 segments
D7 d7(D7::COMCATHODE);


void setup()
{
  // Broche d'entrée pour le bouton poussoir
  pinMode(ledPin, OUTPUT);
  pinMode(swPin, INPUT);
  
  // Connection des broches de l'arduino
  // aux broches de l'afficheur.
  d7.initPin(D7::Seg_A, 7);
  d7.initPin(D7::Seg_B, 8);
  d7.initPin(D7::Seg_C, 6);
  d7.initPin(D7::Seg_D, 4);
  d7.initPin(D7::Seg_E, 2);
  d7.initPin(D7::Seg_F, 5);
  d7.initPin(D7::Seg_G, 3);
  d7.initPin(D7::Seg_P, 9);
  
  // Initialisation de l'aléatoire  
  randomSeed(analogRead(0));
}



// Random
int randomNumber = 0;


void loop()
{
  if (digitalRead(swPin) == HIGH) {
    digitalWrite(ledPin, LOW);
    randomNumber = random(0xF + 1);
  }
  
  else {
    d7.display(randomNumber);
    if (digitalRead(swPin) == LOW) {
      digitalWrite(ledPin, HIGH);
    }
  }
}
